// Logisim project finished_project.circ as structural Verilog: 1 circuit, main circuit main
// 8
module main (
);

  wire button_1_out, button_2_out, clock_1_out, decoder_1_out0, decoder_1_out1, decoder_1_out2,
       decoder_1_out3, decoder_1_out4, decoder_1_out5, decoder_1_out6, decoder_1_out7, or_1_out;
  wire [2:0] counter_1_q, random_1_out;
  wire [7:0] decoder_2_out0, shift_register_1_q7, shift_register_2_q7, shift_register_3_q7,
       shift_register_4_q7, shift_register_5_q7, shift_register_6_q7, shift_register_7_q7,
       shift_register_8_q7;

  Clock clock_1 (.out(clock_1_out));
  Random #(.width(3)) random_1 (.clk(clock_1_out), .out(random_1_out));  // open: next, clr
  Decoder #(.select(3)) decoder_1 (
    .out0(decoder_1_out0), .out1(decoder_1_out1), .out2(decoder_1_out2), .out3(decoder_1_out3),
    .out4(decoder_1_out4), .out5(decoder_1_out5), .out6(decoder_1_out6), .out7(decoder_1_out7),
    .sel(random_1_out));  // open: en
  Shift_Register shift_register_1 (
    .clk(clock_1_out), .load(clock_1_out), .d0(decoder_1_out0), .q0(shift_register_1_q7[7]),
    .d1(decoder_1_out1), .q1(shift_register_1_q7[6]), .d2(decoder_1_out2), .q2(shift_register_1_q7[5]),
    .d3(decoder_1_out3), .q3(shift_register_1_q7[4]), .d4(decoder_1_out4), .q4(shift_register_1_q7[3]),
    .d5(decoder_1_out5), .q5(shift_register_1_q7[2]), .d6(decoder_1_out6), .q6(shift_register_1_q7[1]),
    .d7(decoder_1_out7), .q7(shift_register_1_q7[0]));  // open: shift, in, out, clr
  Shift_Register shift_register_2 (
    .clk(clock_1_out), .load(clock_1_out), .d0(shift_register_1_q7[7]), .q0(shift_register_2_q7[7]),
    .d1(shift_register_1_q7[6]), .q1(shift_register_2_q7[6]), .d2(shift_register_1_q7[5]),
    .q2(shift_register_2_q7[5]), .d3(shift_register_1_q7[4]), .q3(shift_register_2_q7[4]),
    .d4(shift_register_1_q7[3]), .q4(shift_register_2_q7[3]), .d5(shift_register_1_q7[2]),
    .q5(shift_register_2_q7[2]), .d6(shift_register_1_q7[1]), .q6(shift_register_2_q7[1]),
    .d7(shift_register_1_q7[0]), .q7(shift_register_2_q7[0]));  // open: shift, in, out, clr
  Shift_Register shift_register_3 (
    .clk(clock_1_out), .load(clock_1_out), .d0(shift_register_2_q7[7]), .q0(shift_register_3_q7[7]),
    .d1(shift_register_2_q7[6]), .q1(shift_register_3_q7[6]), .d2(shift_register_2_q7[5]),
    .q2(shift_register_3_q7[5]), .d3(shift_register_2_q7[4]), .q3(shift_register_3_q7[4]),
    .d4(shift_register_2_q7[3]), .q4(shift_register_3_q7[3]), .d5(shift_register_2_q7[2]),
    .q5(shift_register_3_q7[2]), .d6(shift_register_2_q7[1]), .q6(shift_register_3_q7[1]),
    .d7(shift_register_2_q7[0]), .q7(shift_register_3_q7[0]));  // open: shift, in, out, clr
  Shift_Register shift_register_4 (
    .clk(clock_1_out), .load(clock_1_out), .d0(shift_register_3_q7[7]), .q0(shift_register_4_q7[7]),
    .d1(shift_register_3_q7[6]), .q1(shift_register_4_q7[6]), .d2(shift_register_3_q7[5]),
    .q2(shift_register_4_q7[5]), .d3(shift_register_3_q7[4]), .q3(shift_register_4_q7[4]),
    .d4(shift_register_3_q7[3]), .q4(shift_register_4_q7[3]), .d5(shift_register_3_q7[2]),
    .q5(shift_register_4_q7[2]), .d6(shift_register_3_q7[1]), .q6(shift_register_4_q7[1]),
    .d7(shift_register_3_q7[0]), .q7(shift_register_4_q7[0]));  // open: shift, in, out, clr
  Shift_Register shift_register_5 (
    .clk(clock_1_out), .load(clock_1_out), .d0(shift_register_4_q7[7]), .q0(shift_register_5_q7[7]),
    .d1(shift_register_4_q7[6]), .q1(shift_register_5_q7[6]), .d2(shift_register_4_q7[5]),
    .q2(shift_register_5_q7[5]), .d3(shift_register_4_q7[4]), .q3(shift_register_5_q7[4]),
    .d4(shift_register_4_q7[3]), .q4(shift_register_5_q7[3]), .d5(shift_register_4_q7[2]),
    .q5(shift_register_5_q7[2]), .d6(shift_register_4_q7[1]), .q6(shift_register_5_q7[1]),
    .d7(shift_register_4_q7[0]), .q7(shift_register_5_q7[0]));  // open: shift, in, out, clr
  Shift_Register shift_register_6 (
    .clk(clock_1_out), .load(clock_1_out), .d0(shift_register_5_q7[7]), .q0(shift_register_6_q7[7]),
    .d1(shift_register_5_q7[6]), .q1(shift_register_6_q7[6]), .d2(shift_register_5_q7[5]),
    .q2(shift_register_6_q7[5]), .d3(shift_register_5_q7[4]), .q3(shift_register_6_q7[4]),
    .d4(shift_register_5_q7[3]), .q4(shift_register_6_q7[3]), .d5(shift_register_5_q7[2]),
    .q5(shift_register_6_q7[2]), .d6(shift_register_5_q7[1]), .q6(shift_register_6_q7[1]),
    .d7(shift_register_5_q7[0]), .q7(shift_register_6_q7[0]));  // open: shift, in, out, clr
  Shift_Register shift_register_7 (
    .clk(clock_1_out), .load(clock_1_out), .d0(shift_register_6_q7[7]), .q0(shift_register_7_q7[7]),
    .d1(shift_register_6_q7[6]), .q1(shift_register_7_q7[6]), .d2(shift_register_6_q7[5]),
    .q2(shift_register_7_q7[5]), .d3(shift_register_6_q7[4]), .q3(shift_register_7_q7[4]),
    .d4(shift_register_6_q7[3]), .q4(shift_register_7_q7[3]), .d5(shift_register_6_q7[2]),
    .q5(shift_register_7_q7[2]), .d6(shift_register_6_q7[1]), .q6(shift_register_7_q7[1]),
    .d7(shift_register_6_q7[0]), .q7(shift_register_7_q7[0]));  // open: shift, in, out, clr
  Shift_Register shift_register_8 (
    .clk(clock_1_out), .load(clock_1_out), .d0(shift_register_7_q7[7]), .q0(shift_register_8_q7[7]),
    .d1(shift_register_7_q7[6]), .q1(shift_register_8_q7[6]), .d2(shift_register_7_q7[5]),
    .q2(shift_register_8_q7[5]), .d3(shift_register_7_q7[4]), .q3(shift_register_8_q7[4]),
    .d4(shift_register_7_q7[3]), .q4(shift_register_8_q7[3]), .d5(shift_register_7_q7[2]),
    .q5(shift_register_8_q7[2]), .d6(shift_register_7_q7[1]), .q6(shift_register_8_q7[1]),
    .d7(shift_register_7_q7[0]), .q7(shift_register_8_q7[0]));  // open: shift, in, out, clr
  Decoder #(.select(3)) decoder_2 (
    .out0(decoder_2_out0[0]), .out1(decoder_2_out0[1]), .out2(decoder_2_out0[2]), .out3(decoder_2_out0[3]),
    .out4(decoder_2_out0[4]), .out5(decoder_2_out0[5]), .out6(decoder_2_out0[6]), .out7(decoder_2_out0[7]),
    .sel(counter_1_q));  // open: en
  Counter #(.width(3), .max('h7)) counter_1 (
    .load(button_1_out), .count(or_1_out), .Q(counter_1_q), .clk(or_1_out));  // open: D, carry, clr
  or or_1 (or_1_out, button_2_out, button_1_out);
  Button button_1 (.out(button_1_out));
  Button button_2 (.out(button_2_out));
  DotMatrix #(.inputtype("row"), .matrixcols(8), .matrixrows(8)) dotmatrix_1 (
    .row0(shift_register_1_q7), .row1(shift_register_2_q7), .row2(shift_register_3_q7),
    .row3(shift_register_4_q7), .row4(shift_register_5_q7), .row5(shift_register_6_q7),
    .row6(shift_register_7_q7), .row7(decoder_2_out0));
endmodule
